# Fritzing sketch nucucar.sensors (saved by Fritzing 0.9.2b)

parts:
  Raspberry_Pi1 = Raspberry Pi B+
  Part1 = Adafruit BME680

nets:
  3V3: Raspberry_Pi1.3v3, Raspberry_Pi1.3V3, Part1.VIN
  N1: Raspberry_Pi1.GPIO2, Part1.SDI/SDA
  N2: Raspberry_Pi1.GPIO3, Part1.SCK/SCL
  GND: Raspberry_Pi1.GND, Part1.GND
